// Logisim project PopCornBoard.circ as structural Verilog: 9 circuits, main circuit MAIN
module MAIN (
  input  [15:0] in_1,
  input  in_2,
  input  [15:0] in_3,
  input  in_4,
  input  [15:0] in_5,
  input  in_6,
  input  [15:0] in_7,
  input  in_8,
  input  in_9,
  output [15:0] out_10,
  output [15:0] out_11,
  output [15:0] out_12,
  output [15:0] out_13,
  output [7:0] out_14,
  output [15:0] out_15,
  output [15:0] out_16,
  output [15:0] out_17,
  output [15:0] out_18,
  output [15:0] out_19,
  output [7:0] out_20,
  output [15:0] out_21,
  output [15:0] out_22,
  output [6:0] out_23,
  output [3:0] out_24,
  output [15:0] out_25,
  output [15:0] out_26,
  output [15:0] out_27,
  output [15:0] out_28,
  output [15:0] out_29,
  output [15:0] out_30,
  output [15:0] out_31,
  output [15:0] out_32,
  output [15:0] out_33
);

  wire ADDE, ADWE, ANDE, AOE, ARE, BRE, button_1_out, button_2_out, CE, CLK, CLRINT, CWE, FLAGE, HLT, I,
       inst_decoder_1_ce, INSTDONE, INSTWE1, INSTWE2, INT, IWE, JMP, MOE, MR, MRM, MWE, OPOE, PCOE, PINTE,
       POE, ports_1_p0i, ports_1_p1i, ports_1_p2i, ports_1_p3i, PTADWE, PTOE, PTWE, PWE, RADWE, ROE, RWE,
       SCE, SDU, SPE, SPOE, SUBE, SWE, XORE;
  wire [1:0] SHE;
  wire [2:0] OP;
  wire [3:0] FLAG, FLAGS;
  wire [31:0] INTDAT;
  wire [47:0] inst_decoder_1_control_word;
  wire [47:20] pull_resistor_1_node;

  LED led_1 (.in(out_17[15]));
  LED led_2 (.in(out_21[15]));
  LED led_3 (.in(out_27[15]));
  LED led_4 (.in(out_29[15]));
  LED led_5 (.in(out_14[7]));
  LED led_6 (.in(out_17[14]));
  LED led_7 (.in(out_17[13]));
  LED led_8 (.in(out_17[12]));
  LED led_9 (.in(out_17[11]));
  LED led_10 (.in(out_21[14]));
  LED led_11 (.in(out_21[13]));
  LED led_12 (.in(out_21[12]));
  LED led_13 (.in(out_21[11]));
  LED led_14 (.in(out_27[14]));
  LED led_15 (.in(out_27[13]));
  LED led_16 (.in(out_27[12]));
  LED led_17 (.in(out_27[11]));
  LED led_18 (.in(out_29[14]));
  LED led_19 (.in(out_29[13]));
  LED led_20 (.in(out_29[12]));
  LED led_21 (.in(out_29[11]));
  LED led_22 (.in(out_14[6]));
  LED led_23 (.in(out_14[5]));
  LED led_24 (.in(out_14[4]));
  LED led_25 (.in(out_14[3]));
  LED led_26 (.in(out_17[10]));
  LED led_27 (.in(out_17[9]));
  LED led_28 (.in(out_17[8]));
  LED led_29 (.in(out_17[7]));
  LED led_30 (.in(out_21[10]));
  LED led_31 (.in(out_21[9]));
  LED led_32 (.in(out_21[8]));
  LED led_33 (.in(out_21[7]));
  LED led_34 (.in(out_27[10]));
  LED led_35 (.in(out_27[9]));
  LED led_36 (.in(out_27[8]));
  LED led_37 (.in(out_27[7]));
  LED led_38 (.in(out_29[10]));
  LED led_39 (.in(out_29[9]));
  LED led_40 (.in(out_29[8]));
  LED led_41 (.in(out_29[7]));
  and and_1 (CE, pull_resistor_1_node[20], inst_decoder_1_ce);
  assign MR = pull_resistor_1_node[36] ? pull_resistor_1_node[36] : 1'bz;  // Controlled_Buffer controlled_buffer_1
  LED led_42 (.in(out_14[2]));
  LED led_43 (.in(out_14[1]));
  LED led_44 (.in(out_14[0]));
  LED led_45 (.in(out_17[6]));
  LED led_46 (.in(out_17[5]));
  LED led_47 (.in(out_17[4]));
  LED led_48 (.in(out_17[3]));
  LED led_49 (.in(out_21[6]));
  LED led_50 (.in(out_21[5]));
  LED led_51 (.in(out_21[4]));
  LED led_52 (.in(out_21[3]));
  LED led_53 (.in(out_27[6]));
  LED led_54 (.in(out_27[5]));
  LED led_55 (.in(out_27[4]));
  LED led_56 (.in(out_27[3]));
  LED led_57 (.in(out_29[6]));
  LED led_58 (.in(out_29[5]));
  LED led_59 (.in(out_29[4]));
  LED led_60 (.in(out_29[3]));
  Pull_Resistor pull_resistor_1 (.node({pull_resistor_1_node[47:42], PTOE, PTWE, PTADWE, PINTE, CLRINT, pull_resistor_1_node[36], CWE, IWE, POE, PWE, FLAGE, PCOE, HLT, INSTWE2, INSTWE1, INSTDONE, OPOE, OP, ROE, pull_resistor_1_node[20], JMP, RADWE, RWE, SPOE, SDU, SWE, SCE, SPE, MOE, ADWE, MWE, AOE, SHE, XORE, ANDE, SUBE, ADDE, BRE, ARE}));
  assign {pull_resistor_1_node[47:42], PTOE, PTWE, PTADWE, PINTE, CLRINT, pull_resistor_1_node[36], CWE, IWE, POE, PWE, FLAGE, PCOE, HLT, INSTWE2, INSTWE1, INSTDONE, OPOE, OP, ROE, pull_resistor_1_node[20], JMP, RADWE, RWE, SPOE, SDU, SWE, SCE, SPE, MOE, ADWE, MWE, AOE, SHE, XORE, ANDE, SUBE, ADDE, BRE, ARE} = inst_decoder_1_control_word;  // Buffer buffer_1, 48 bits wide
  LED led_61 (.in(out_15[15]));
  LED led_62 (.in(out_17[2]));
  LED led_63 (.in(out_17[1]));
  LED led_64 (.in(out_17[0]));
  LED led_65 (.in(out_18[15]));
  LED led_66 (.in(out_21[2]));
  LED led_67 (.in(out_21[1]));
  LED led_68 (.in(out_21[0]));
  LED led_69 (.in(out_22[15]));
  LED led_70 (.in(out_27[2]));
  LED led_71 (.in(out_27[1]));
  LED led_72 (.in(out_27[0]));
  LED led_73 (.in(out_28[15]));
  LED led_74 (.in(out_29[2]));
  LED led_75 (.in(out_29[1]));
  LED led_76 (.in(out_29[0]));
  LED led_77 (.in(out_30[15]));
  LED led_78 (.in(out_31[15]));
  LED led_79 (.in(out_32[15]));
  LED led_80 (.in(out_33[15]));
  LED led_81 (.in(out_15[14]));
  LED led_82 (.in(out_15[13]));
  LED led_83 (.in(out_15[12]));
  LED led_84 (.in(out_15[11]));
  LED led_85 (.in(out_18[14]));
  LED led_86 (.in(out_18[13]));
  LED led_87 (.in(out_18[12]));
  LED led_88 (.in(out_18[11]));
  LED led_89 (.in(out_22[14]));
  LED led_90 (.in(out_22[13]));
  LED led_91 (.in(out_22[12]));
  LED led_92 (.in(out_22[11]));
  LED led_93 (.in(out_28[14]));
  LED led_94 (.in(out_28[13]));
  LED led_95 (.in(out_28[12]));
  LED led_96 (.in(out_28[11]));
  LED led_97 (.in(out_30[14]));
  LED led_98 (.in(out_30[13]));
  LED led_99 (.in(out_30[12]));
  LED led_100 (.in(out_30[11]));
  LED led_101 (.in(out_31[14]));
  LED led_102 (.in(out_31[13]));
  LED led_103 (.in(out_31[12]));
  LED led_104 (.in(out_31[11]));
  LED led_105 (.in(out_32[14]));
  LED led_106 (.in(out_32[13]));
  LED led_107 (.in(out_32[12]));
  LED led_108 (.in(out_32[11]));
  LED led_109 (.in(out_33[14]));
  LED led_110 (.in(out_33[13]));
  LED led_111 (.in(out_33[12]));
  LED led_112 (.in(out_33[11]));
  REG reg_1 (
    .JMP(JMP), .CE(CE), .PCOE(PCOE), .RWE(RWE), .ROE(ROE), .RIN(out_16), .RADWE(RADWE), .POE(POE), .PWE(PWE),
    .FLAGE(FLAGE), .FLAGS(FLAGS), .CWE(CWE), .IWE(IWE), .CLK(CLK), .MR(MR), .PC(out_21), .AD(out_17),
    .IOUT(I), .FLAG(FLAG), .P(out_14), .H(out_33), .A(out_15), .B(out_18), .C(out_22), .D(out_28),
    .E(out_30), .F(out_31), .G(out_32), .DATAOUT(out_16));
  LED led_113 (.in(out_15[10]));
  LED led_114 (.in(out_15[9]));
  LED led_115 (.in(out_15[8]));
  LED led_116 (.in(out_15[7]));
  LED led_117 (.in(out_18[10]));
  LED led_118 (.in(out_18[9]));
  LED led_119 (.in(out_18[8]));
  LED led_120 (.in(out_18[7]));
  LED led_121 (.in(out_22[10]));
  LED led_122 (.in(out_22[9]));
  LED led_123 (.in(out_22[8]));
  LED led_124 (.in(out_22[7]));
  LED led_125 (.in(out_28[10]));
  LED led_126 (.in(out_28[9]));
  LED led_127 (.in(out_28[8]));
  LED led_128 (.in(out_28[7]));
  LED led_129 (.in(out_30[10]));
  LED led_130 (.in(out_30[9]));
  LED led_131 (.in(out_30[8]));
  LED led_132 (.in(out_30[7]));
  LED led_133 (.in(out_31[10]));
  LED led_134 (.in(out_31[9]));
  LED led_135 (.in(out_31[8]));
  LED led_136 (.in(out_31[7]));
  LED led_137 (.in(out_32[10]));
  LED led_138 (.in(out_32[9]));
  LED led_139 (.in(out_32[8]));
  LED led_140 (.in(out_32[7]));
  LED led_141 (.in(out_33[10]));
  LED led_142 (.in(out_33[9]));
  LED led_143 (.in(out_33[8]));
  LED led_144 (.in(out_33[7]));
  INST_DECODER inst_decoder_1 (
    .OPERAND(OP), .OPERAND_OE(OPOE), .INST_DONE(INSTDONE), .FLAGS(FLAG), .INT(INT), .I(I), .INTDAT(INTDAT),
    .INSTWE2(INSTWE2), .INST_IN(out_16), .INSTWE1(INSTWE1), .CLK(CLK), .MR(MRM), .INST2(out_29),
    .INST1(out_27), .INST_OUT(out_16), .INST_STEP(out_24), .OPCODE(out_23),
    .CONTROL_WORD(inst_decoder_1_control_word), .CE(inst_decoder_1_ce));
  LED led_145 (.in(out_15[6]));
  LED led_146 (.in(out_15[5]));
  LED led_147 (.in(out_15[4]));
  LED led_148 (.in(out_15[3]));
  LED led_149 (.in(out_18[6]));
  LED led_150 (.in(out_18[5]));
  LED led_151 (.in(out_18[4]));
  LED led_152 (.in(out_18[3]));
  LED led_153 (.in(out_22[6]));
  LED led_154 (.in(out_22[5]));
  LED led_155 (.in(out_22[4]));
  LED led_156 (.in(out_22[3]));
  LED led_157 (.in(out_28[6]));
  LED led_158 (.in(out_28[5]));
  LED led_159 (.in(out_28[4]));
  LED led_160 (.in(out_28[3]));
  LED led_161 (.in(out_30[6]));
  LED led_162 (.in(out_30[5]));
  LED led_163 (.in(out_30[4]));
  LED led_164 (.in(out_30[3]));
  LED led_165 (.in(out_31[6]));
  LED led_166 (.in(out_31[5]));
  LED led_167 (.in(out_31[4]));
  LED led_168 (.in(out_31[3]));
  LED led_169 (.in(out_32[6]));
  LED led_170 (.in(out_32[5]));
  LED led_171 (.in(out_32[4]));
  LED led_172 (.in(out_32[3]));
  LED led_173 (.in(out_33[6]));
  LED led_174 (.in(out_33[5]));
  LED led_175 (.in(out_33[4]));
  LED led_176 (.in(out_33[3]));
  LED led_177 (.in(out_15[2]));
  LED led_178 (.in(out_15[1]));
  LED led_179 (.in(out_15[0]));
  LED led_180 (.in(out_18[2]));
  LED led_181 (.in(out_18[1]));
  LED led_182 (.in(out_18[0]));
  LED led_183 (.in(out_22[2]));
  LED led_184 (.in(out_22[1]));
  LED led_185 (.in(out_22[0]));
  LED led_186 (.in(out_28[2]));
  LED led_187 (.in(out_28[1]));
  LED led_188 (.in(out_28[0]));
  LED led_189 (.in(out_30[2]));
  LED led_190 (.in(out_30[1]));
  LED led_191 (.in(out_30[0]));
  LED led_192 (.in(out_31[2]));
  LED led_193 (.in(out_31[1]));
  LED led_194 (.in(out_31[0]));
  LED led_195 (.in(out_32[2]));
  LED led_196 (.in(out_32[1]));
  LED led_197 (.in(out_32[0]));
  LED led_198 (.in(out_33[2]));
  LED led_199 (.in(out_33[1]));
  LED led_200 (.in(out_33[0]));
  INTERRUPT interrupt_1 (
    .CLK(CLK), .MR(MR), .INT_IN(out_16), .I(I), .PINTE(PINTE), .P0(ports_1_p0i), .P1(ports_1_p1i),
    .P2(ports_1_p2i), .P3(ports_1_p3i), .CLR(CLRINT), .INT(INT), .DATA(INTDAT));
  LED led_201 (.in(out_16[15]));
  LED led_202 (.in(out_16[14]));
  LED led_203 (.in(out_16[13]));
  LED led_204 (.in(out_23[0]));
  LED led_205 (.in(out_23[1]));
  Pull_Resistor pull_resistor_2 (.node(MR));
  assign MR = button_1_out ? button_1_out : 1'bz;  // Controlled_Buffer controlled_buffer_2
  LED led_206 (.in(out_16[12]));
  LED led_207 (.in(out_16[11]));
  LED led_208 (.in(out_16[10]));
  LED led_209 (.in(out_16[9]));
  LED led_210 (.in(out_23[2]));
  LED led_211 (.in(out_23[3]));
  LED led_212 (.in(out_23[4]));
  LED led_213 (.in(out_23[5]));
  buf buffer_2 (MRM, button_1_out);
  THE_CLOCK the_clock_1 (.SINGLE_STEP_IN(button_2_out), .SINGLE_STEP(in_9), .HLT(HLT), .CLK(CLK));  // open: nCLK
  Button button_1 (.out(button_1_out));
  Button button_2 (.out(button_2_out));
  Pull_Resistor pull_resistor_3 (.node(out_16));
  LED led_214 (.in(out_16[8]));
  LED led_215 (.in(out_16[7]));
  LED led_216 (.in(out_16[6]));
  LED led_217 (.in(out_16[5]));
  LED led_218 (.in(out_23[6]));
  LED led_219 (.in(out_24[3]));
  LED led_220 (.in(out_24[2]));
  LED led_221 (.in(out_16[4]));
  LED led_222 (.in(out_16[3]));
  LED led_223 (.in(out_16[2]));
  LED led_224 (.in(out_16[1]));
  LED led_225 (.in(out_24[1]));
  LED led_226 (.in(out_24[0]));
  LED led_227 (.in(out_16[0]));
  LED led_228 (.in(out_19[15]));
  LED led_229 (.in(out_25[15]));
  ALU alu_1 (
    .ALUoe(AOE), .A_REGe(ARE), .B_REGe(BRE), .BUSin_ALU(out_16), .CLK(CLK), .MR(MR), .SUBe(SUBE),
    .XORe(XORE), .ANDe(ANDE), .ADDe(ADDE), .SHIFT(SHE), .VF(FLAGS[3]), .NF(FLAGS[2]), .CF(FLAGS[0]),
    .ZF(FLAGS[1]), .BUSout_ALU(out_16), .REG_Bo(out_25), .REG_Ao(out_19));
  PORTS ports_1 (
    .MR(MR), .CLK(CLK), .PWE(PTWE), .PADWE(PTADWE), .POE(PTOE), .PORTIN(out_16), .P3D(in_7), .P0D(in_1),
    .P1D(in_5), .P2D(in_3), .P3WE(in_8), .P0WE(in_2), .P1WE(in_6), .P2WE(in_4), .P3Q(out_13), .P0Q(out_10),
    .P1Q(out_12), .P2Q(out_11), .P0I(ports_1_p0i), .P1I(ports_1_p1i), .P2I(ports_1_p2i), .P3I(ports_1_p3i),
    .POUT(out_16));
  LED led_230 (.in(out_19[14]));
  LED led_231 (.in(out_19[13]));
  LED led_232 (.in(out_19[12]));
  LED led_233 (.in(out_19[11]));
  LED led_234 (.in(out_25[14]));
  LED led_235 (.in(out_25[13]));
  LED led_236 (.in(out_25[12]));
  LED led_237 (.in(out_25[11]));
  MEMORY_UNIT memory_unit_1 (
    .MOE(MOE), .SPOE(SPOE), .SPE(SPE), .SWE(SWE), .ADWE(ADWE), .MWE(MWE), .D_U(SDU), .CE(SCE), .CLK(CLK),
    .MR(MR), .MEMIN(out_16), .SP(out_20), .MEMAD(out_26), .MEMOUT(out_16));
  LED led_238 (.in(FLAGS[3]));
  LED led_239 (.in(FLAGS[2]));
  LED led_240 (.in(FLAGS[1]));
  LED led_241 (.in(out_19[10]));
  LED led_242 (.in(out_19[9]));
  LED led_243 (.in(out_19[8]));
  LED led_244 (.in(out_19[7]));
  LED led_245 (.in(out_25[10]));
  LED led_246 (.in(out_25[9]));
  LED led_247 (.in(out_25[8]));
  LED led_248 (.in(out_25[7]));
  LED led_249 (.in(FLAGS[0]));
  LED led_250 (.in(out_19[6]));
  LED led_251 (.in(out_19[5]));
  LED led_252 (.in(out_19[4]));
  LED led_253 (.in(out_19[3]));
  LED led_254 (.in(out_25[6]));
  LED led_255 (.in(out_25[5]));
  LED led_256 (.in(out_25[4]));
  LED led_257 (.in(out_25[3]));
  LED led_258 (.in(out_19[2]));
  LED led_259 (.in(out_19[1]));
  LED led_260 (.in(out_19[0]));
  LED led_261 (.in(out_25[2]));
  LED led_262 (.in(out_25[1]));
  LED led_263 (.in(out_25[0]));
  LED led_264 (.in(out_26[15]));
  LED led_265 (.in(out_26[14]));
  LED led_266 (.in(out_20[7]));
  LED led_267 (.in(out_20[6]));
  LED led_268 (.in(out_26[13]));
  LED led_269 (.in(out_26[12]));
  LED led_270 (.in(out_26[11]));
  LED led_271 (.in(out_26[10]));
  LED led_272 (.in(out_20[5]));
  LED led_273 (.in(out_20[4]));
  LED led_274 (.in(out_20[3]));
  LED led_275 (.in(out_20[2]));
  LED led_276 (.in(out_26[9]));
  LED led_277 (.in(out_26[8]));
  LED led_278 (.in(out_26[7]));
  LED led_279 (.in(out_26[6]));
  LED led_280 (.in(out_20[1]));
  LED led_281 (.in(out_20[0]));
  LED led_282 (.in(out_26[5]));
  LED led_283 (.in(out_26[4]));
  LED led_284 (.in(out_26[3]));
  LED led_285 (.in(out_26[2]));
  LED led_286 (.in(out_26[1]));
  LED led_287 (.in(out_26[0]));

  // Other names for the same wires on the sheet: A[15:0] = out_15; ALU_A[15:0] = out_19; ALU_B[15:0] = out_25;
  //   B[15:0] = out_18; C[15:0] = out_22; D[15:0] = out_28; E[15:0] = out_30; F[15:0] = out_31; G[15:0] = out_32;
  //   H[15:0] = out_33; INST1[15:0] = out_27; ISNT2[15:0] = out_29; MEMAD[15:0] = out_26; OPCODE[6:0] = out_23;
  //   P[7:0] = out_14; PC[15:0] = out_21; RDT[15:0] = out_17; STACK[7:0] = out_20; STEP[3:0] = out_24

  // Notes on the sheet:
  //   BUS
  //   VF NF ZF CF
endmodule

module ALU (
  input  [15:0] BUSin_ALU,
  input  [1:0] SHIFT,
  input  A_REGe,
  input  B_REGe,
  input  CLK,
  input  MR,
  input  SUBe,
  input  XORe,
  input  ANDe,
  input  ADDe,
  input  ALUoe,
  output [15:0] REG_Bo,
  output [15:0] REG_Ao,
  output VF,
  output NF,
  output CF,
  output ZF,
  output [15:0] BUSout_ALU
);

  wire and_2_out, and_3_out;
  wire [14:0] adder_1_out;
  wire [15:0] and_1_out, bit_extender_1_out, controlled_buffer_1_out, controlled_buffer_2_out,
       controlled_buffer_3_out, multiplexer_1_out, or_1_out, xor_1_out, xor_2_out;

  Pull_Resistor pull_resistor_1 (.node(REG_Bo));
  Register #(.width(16)) REG_A (.D(BUSin_ALU), .en(A_REGe), .clk(CLK), .Q(REG_Ao), .clr(MR));
  Register #(.width(16)) REG_B (.D(BUSin_ALU), .en(B_REGe), .clk(CLK), .Q(REG_Bo), .clr(MR));
  Pull_Resistor pull_resistor_2 (.node(REG_Ao));
  assign xor_1_out = REG_Ao ^ REG_Bo;  // XOR_Gate xor_1, 16 bits wide
  assign and_1_out = REG_Ao & REG_Bo;  // AND_Gate and_1, 16 bits wide
  assign xor_2_out = REG_Bo ^ bit_extender_1_out;  // XOR_Gate xor_2, 16 bits wide
  assign bit_extender_1_out = {{15{SUBe}}, SUBe};  // Bit_Extender bit_extender_1
  Adder #(.width(16)) adder_1 (.a(REG_Ao), .b(xor_2_out), .out({NF, adder_1_out}), .cin(SUBe), .cout(CF));
  assign controlled_buffer_1_out = XORe ? xor_1_out : 16'bz;  // Controlled_Buffer controlled_buffer_1
  assign controlled_buffer_2_out = ANDe ? and_1_out : 16'bz;  // Controlled_Buffer controlled_buffer_2
  assign controlled_buffer_3_out = ADDe ? {NF, adder_1_out} : 16'bz;  // Controlled_Buffer controlled_buffer_3
  and and_2 (and_2_out, REG_Ao[15], xor_2_out[15], ~NF);  // AND_Gate
  Pull_Resistor pull_resistor_3 (.node(controlled_buffer_1_out));
  Pull_Resistor pull_resistor_4 (.node(controlled_buffer_2_out));
  assign or_1_out = controlled_buffer_1_out | controlled_buffer_2_out | controlled_buffer_3_out;  // OR_Gate or_1, 16 bits wide
  Pull_Resistor pull_resistor_5 (.node(controlled_buffer_3_out));
  and and_3 (and_3_out, ~REG_Ao[15], ~xor_2_out[15], NF);  // AND_Gate
  or or_2 (VF, and_3_out, and_2_out);
  // NoConnect on or_1_out[0]
  Multiplexer #(.select(2), .width(16)) multiplexer_1 (
    .in0(or_1_out), .in1({1'b0, or_1_out[15:1]}), .in2({or_1_out[0], or_1_out[15:1]}),
    .in3({or_1_out[14:0], or_1_out[15]}), .out(multiplexer_1_out), .sel(SHIFT));
  nor nor_1 (ZF, multiplexer_1_out[15], multiplexer_1_out[14], multiplexer_1_out[13], multiplexer_1_out[12], multiplexer_1_out[11], multiplexer_1_out[10], multiplexer_1_out[9], multiplexer_1_out[8], multiplexer_1_out[7], multiplexer_1_out[6], multiplexer_1_out[5], multiplexer_1_out[4], multiplexer_1_out[3], multiplexer_1_out[2], multiplexer_1_out[1], multiplexer_1_out[0]);
  assign BUSout_ALU = ALUoe ? multiplexer_1_out : 16'bz;  // Controlled_Buffer controlled_buffer_4
endmodule

module REG (
  input  PCOE,
  input  RWE,
  input  ROE,
  input  JMP,
  input  CE,
  input  CLK,
  input  MR,
  input  [15:0] RIN,
  input  RADWE,
  input  POE,
  input  PWE,
  input  FLAGE,
  input  [3:0] FLAGS,
  input  CWE,
  input  IWE,
  output [15:0] PC,
  output [15:0] A,
  output [15:0] DATAOUT,
  output [15:0] B,
  output [15:0] AD,
  output [15:0] C,
  output [3:0] FLAG,
  output [15:0] D,
  output [7:0] P,
  output [15:0] E,
  output [15:0] F,
  output IOUT,
  output [15:0] G,
  output [15:0] H
);

  wire and_1_out, and_2_out, and_3_out, decoder_1_out0, decoder_1_out1, decoder_1_out2, decoder_1_out3,
       decoder_1_out4, decoder_1_out5, decoder_1_out6, decoder_1_out7, not_1_out, not_2_out;
  wire [2:0] bit_extender_1_out;
  wire [4:0] STATUS_q;
  wire [15:0] bit_extender_2_out, controlled_buffer_1_out, controlled_buffer_4_out;

  Register #(.width(16)) register_1 (.D(RIN), .en(RADWE), .clk(CLK), .Q(AD), .clr(MR));
  assign controlled_buffer_1_out[3:0] = FLAGE ? FLAGS : 4'bz;  // Controlled_Buffer controlled_buffer_1
  Counter #(.max('hffff), .width(16)) counter_1 (
    .load(JMP), .D(RIN), .count(CE), .Q(PC), .up(1'b1), .clk(CLK), .clr(MR));  // open: carry
  not not_1 (not_1_out, FLAGE);
  assign controlled_buffer_1_out = not_1_out ? RIN : 16'bz;  // Controlled_Buffer controlled_buffer_2
  assign DATAOUT = PCOE ? PC : 16'bz;  // Controlled_Buffer controlled_buffer_3
  and and_1 (and_1_out, RWE, CLK);
  Register STATUS (
    .D({4'b1111, controlled_buffer_1_out[3:1], 1'b1}), .en(PWE), .clk(CLK),
    .Q({P[7:5], STATUS_q[4], FLAG[3:1], STATUS_q[0]}), .clr(MR));
  D_Flip_Flop CF (.D(controlled_buffer_1_out[0]), .clk(and_2_out), .Q(FLAG[0]), .preset(MR), .reset(MR));  // open: Qn
  and and_2 (and_2_out, CLK, CWE);
  D_Flip_Flop I (.D(RIN[0]), .clk(and_3_out), .Q(IOUT), .preset(MR), .reset(MR));  // open: Qn
  and and_3 (and_3_out, CLK, IWE);
  not not_2 (not_2_out, AD[3]);
  Decoder #(.select(3)) decoder_1 (
    .out0(decoder_1_out0), .out1(decoder_1_out1), .out2(decoder_1_out2), .out3(decoder_1_out3),
    .out4(decoder_1_out4), .out5(decoder_1_out5), .out6(decoder_1_out6), .out7(decoder_1_out7),
    .sel(bit_extender_1_out), .en(not_2_out));
  Bit_Extender #(.in_width(16), .out_width(3)) bit_extender_1 (.in(AD), .out(bit_extender_1_out));
  assign bit_extender_2_out = {{8{1'b0}}, {P[7:5], IOUT, FLAG}};  // Bit_Extender bit_extender_2
  Register #(.width(16)) register_2 (.D(RIN), .en(decoder_1_out0), .clk(and_1_out), .Q(A), .clr(MR));
  Register #(.width(16)) register_3 (.D(RIN), .en(decoder_1_out1), .clk(and_1_out), .Q(B), .clr(MR));
  Register #(.width(16)) register_4 (.D(RIN), .en(decoder_1_out2), .clk(and_1_out), .Q(C), .clr(MR));
  Register #(.width(16)) register_5 (.D(RIN), .en(decoder_1_out3), .clk(and_1_out), .Q(D), .clr(MR));
  assign controlled_buffer_4_out = POE ? bit_extender_2_out : 16'bz;  // Controlled_Buffer controlled_buffer_4
  Register #(.width(16)) register_6 (.D(RIN), .en(decoder_1_out4), .clk(and_1_out), .Q(E), .clr(MR));
  Register #(.width(16)) register_7 (.D(RIN), .en(decoder_1_out5), .clk(and_1_out), .Q(F), .clr(MR));
  Register #(.width(16)) register_8 (.D(RIN), .en(decoder_1_out6), .clk(and_1_out), .Q(G), .clr(MR));
  Register #(.width(16)) register_9 (.D(RIN), .en(decoder_1_out7), .clk(and_1_out), .Q(H), .clr(MR));
  assign controlled_buffer_4_out = decoder_1_out0 ? A : 16'bz;  // Controlled_Buffer controlled_buffer_5
  assign controlled_buffer_4_out = decoder_1_out1 ? B : 16'bz;  // Controlled_Buffer controlled_buffer_6
  assign controlled_buffer_4_out = decoder_1_out2 ? C : 16'bz;  // Controlled_Buffer controlled_buffer_7
  assign controlled_buffer_4_out = decoder_1_out3 ? D : 16'bz;  // Controlled_Buffer controlled_buffer_8
  assign controlled_buffer_4_out = decoder_1_out4 ? E : 16'bz;  // Controlled_Buffer controlled_buffer_9
  assign controlled_buffer_4_out = decoder_1_out5 ? F : 16'bz;  // Controlled_Buffer controlled_buffer_10
  assign controlled_buffer_4_out = decoder_1_out6 ? G : 16'bz;  // Controlled_Buffer controlled_buffer_11
  assign controlled_buffer_4_out = decoder_1_out7 ? H : 16'bz;  // Controlled_Buffer controlled_buffer_12
  assign DATAOUT = ROE ? controlled_buffer_4_out : 16'bz;  // Controlled_Buffer controlled_buffer_13

  assign P[4:0] = {IOUT, FLAG};
endmodule

module INST_DECODER (
  input  INT,
  input  I,
  input  [31:0] INTDAT,
  input  INSTWE2,
  input  [15:0] INST_IN,
  input  INST_DONE,
  input  [3:0] FLAGS,
  input  INSTWE1,
  input  CLK,
  input  MR,
  input  [2:0] OPERAND,
  input  OPERAND_OE,
  output CE,
  output [15:0] INST2,
  output [3:0] INST_STEP,
  output [15:0] INST1,
  output [47:0] CONTROL_WORD,
  output [6:0] OPCODE,
  output [15:0] INST_OUT
);

  wire and_1_out, and_2_out, and_3_out, nor_2_out, nor_3_out, nor_4_out, not_1_out, or_1_out, s_r_ff_1_q;
  wire [15:0] bit_extender_1_out, bit_extender_2_out, bit_extender_3_out, bit_extender_4_out,
       multiplexer_1_out, multiplexer_2_out;

  S_R_Flip_Flop s_r_ff_1 (.S(and_3_out), .R(1'b0), .clk(CLK), .Q(s_r_ff_1_q), .reset(nor_2_out));  // open: Qn, preset
  and and_1 (and_1_out, INT, ~I);  // AND_Gate
  nor nor_1 (CE, and_3_out, and_2_out);
  and and_2 (and_2_out, s_r_ff_1_q, nor_3_out);
  Multiplexer #(.width(16)) multiplexer_1 (
    .in0(INST_IN), .in1(INTDAT[31:16]), .out(multiplexer_1_out), .sel(and_2_out));
  and and_3 (and_3_out, and_1_out, nor_4_out);
  Multiplexer #(.width(16)) multiplexer_2 (.in0(INST_IN), .in1(INTDAT[15:0]), .out(multiplexer_2_out), .sel(and_3_out));
  Register #(.width(16)) register_1 (.D(multiplexer_1_out), .en(INSTWE2), .clk(CLK), .Q(INST2), .clr(MR));
  Register #(.width(16)) register_2 (.D(multiplexer_2_out), .en(INSTWE1), .clk(CLK), .Q(INST1), .clr(MR));
  // NoConnect on INST2[15]
  // NoConnect on INST2[14]
  // NoConnect on INST2[13]
  nor nor_2 (nor_2_out, INST_STEP[0], INST_STEP[1], ~INST_STEP[2], INST_STEP[3]);  // NOR_Gate
  nor nor_3 (nor_3_out, ~INST_STEP[0], ~INST_STEP[1], INST_STEP[2], INST_STEP[3]);  // NOR_Gate
  nor nor_4 (nor_4_out, ~INST_STEP[0], INST_STEP[1], INST_STEP[2], INST_STEP[3]);  // NOR_Gate
  assign bit_extender_1_out = {{13{1'b0}}, INST2[12:10]};  // Bit_Extender bit_extender_1
  assign bit_extender_2_out = {{13{1'b0}}, INST1[15:13]};  // Bit_Extender bit_extender_2
  assign bit_extender_3_out = {{13{1'b0}}, INST1[12:10]};  // Bit_Extender bit_extender_3
  assign bit_extender_4_out = {{13{1'b0}}, INST1[9:7]};  // Bit_Extender bit_extender_4
  Multiplexer #(.disabled("Z"), .enable("true"), .select(3), .width(16)) multiplexer_3 (
    .in0(bit_extender_4_out), .in1(bit_extender_3_out), .in2(bit_extender_2_out),
    .in3({INST2[9:0], INST1[15:10]}), .in4({INST2[6:0], INST1[15:7]}), .in5(bit_extender_1_out),
    .in6({16{1'b1}}), .in7({16{1'b0}}), .out(INST_OUT), .sel(OPERAND), .en(OPERAND_OE));
  Counter #(.max('hf), .width(4)) counter_1 (
    .load(1'b0), .count(1'b1), .Q(INST_STEP), .up(1'b1), .clk(not_1_out), .clr(or_1_out));  // open: D, carry
  not not_1 (not_1_out, CLK);
  or or_1 (or_1_out, MR, INST_DONE);
  ROM #(.addrWidth(15), .dataWidth(48)) rom_1 (.addr({INST1[6:0], FLAGS, INST_STEP}), .data(CONTROL_WORD));
  Pull_Resistor pull_resistor_1 (.node({INST1[6:0], FLAGS, INST_STEP}));

  assign OPCODE = INST1[6:0];

  // Notes on the sheet:
  //   contents of rom_1 (hex, n*v repeats v):
  //   40000400 8100800 1980000000 3802400 80800 4000000 10*0 40000400 8100800 1980000000 3802400 80800
  //   4000000 10*0 40000400 8100800 1980000000 3802400 80800 4000000 10*0 40000400 8100800 1980000000
  //   3802400 80800 4000000 10*0 40000400 8100800 1980000000 3802400 80800 4000000 10*0 40000400 8100800
  //   1980000000 3802400 80800 4000000 10*0 40000400 8100800 1980000000 3802400 80800 4000000 10*0
  //   40000400 8100800 1980000000 3802400 80800 4000000 10*0 40000400 8100800 1980000000 3802400 80800
  //   4000000 10*0 40000400 8100800 1980000000 3802400 80800 4000000 10*0 40000400 8100800 1980000000
  //   3802400 80800 4000000 10*0 40000400 8100800 1980000000 3802400 80800 4000000 10*0 40000400 8100800
  //   1980000000 3802400 80800 4000000 10*0 40000400 8100800 1980000000 3802400 80800 4000000 10*0
  //   40000400 8100800 1980000000 3802400 80800 4000000 10*0 40000400 8100800 1980000000 3802400 80800
  //   4000000 10*0 40000400 8100800 24000000 13*0 40000400 8100800 24000000 13*0 40000400 8100800 24000000
  //   13*0 40000400 8100800 24000000 13*0 40000400 8100800 24000000 13*0 40000400 8100800 24000000 13*0
  //   40000400 8100800 24000000 13*0 40000400 8100800 24000000 13*0 40000400 8100800 24000000 13*0
  //   40000400 8100800 24000000 13*0 40000400 8100800 24000000 13*0 40000400 8100800 24000000 13*0
  //   40000400 8100800 24000000 13*0 40000400 8100800 24000000 13*0 40000400 8100800 24000000 13*0
  //   40000400 8100800 24000000 13*0 40000400 8100800 40000400 10100800 2040001200 2000 200001200 2000
  //   3000400 80800 4000000 5*0 40000400 8100800 40000400 10100800 2040001200 2000 200001200 2000 3000400
  //   80800 4000000 5*0 40000400 8100800 40000400 10100800 2040001200 2000 200001200 2000 3000400 80800
  //   4000000 5*0 40000400 8100800 40000400 10100800 2040001200 2000 200001200 2000 3000400 80800 4000000
  //   5*0 40000400 8100800 40000400 10100800 2040001200 2000 200001200 2000 3000400 80800 4000000 5*0
  //   40000400 8100800 40000400 10100800 2040001200 2000 200001200 2000 3000400 80800 4000000 5*0 40000400
  //   8100800 40000400 10100800 2040001200 2000 200001200 2000 3000400 80800 4000000 5*0 40000400 8100800
  //   40000400 10100800 2040001200 2000 200001200 2000 3000400 80800 4000000 5*0 40000400 8100800 40000400
  //   10100800 2040001200 2000 200001200 2000 3000400 80800 4000000 5*0 40000400 8100800 40000400 10100800
  //   2040001200 2000 200001200 2000 3000400 80800 4000000 5*0 40000400 8100800 40000400 10100800
  //   2040001200 2000 200001200 2000 3000400 80800 4000000 5*0 40000400 8100800 40000400 10100800
  //   2040001200 2000 200001200 2000 3000400 80800 4000000 5*0 40000400 8100800 40000400 10100800
  //   2040001200 2000 200001200 2000 3000400 80800 4000000 5*0 40000400 8100800 40000400 10100800
  //   2040001200 2000 200001200 2000 3000400 80800 4000000 5*0 40000400 8100800 40000400 10100800
  //   2040001200 2000 200001200 2000 3000400 80800 4000000 5*0 40000400 8100800 40000400 10100800
  //   2040001200 2000 200001200 2000 3000400 80800 4000000 5*0 40000400 8100800 24000000 13*0 40000400
  //   8100800 24000000 13*0 40000400 8100800 24000000 13*0 40000400 8100800 24000000 13*0 40000400 8100800
  //   24000000 13*0 40000400 8100800 24000000 13*0 40000400 8100800 24000000 13*0 40000400 8100800
  //   24000000 13*0 40000400 8100800 24000000 13*0 40000400 8100800 24000000 13*0 40000400 8100800
  //   24000000 13*0 40000400 8100800 24000000 13*0 40000400 8100800 24000000 13*0 40000400 8100800
  //   24000000 13*0 40000400 8100800 24000000 13*0 40000400 8100800 24000000 13*0 40000400 8100800 2040000
  //   200001 2440000 200002 2840000 880020104 4000000 7*0 40000400 8100800 2040000 200001 2440000 200002
  //   2840000 880020104 4000000 7*0 40000400 8100800 2040000 200001 2440000 200002 2840000 880020104
  //   4000000 7*0 40000400 8100800 2040000 200001 2440000 200002 2840000 880020104 4000000 7*0 40000400
  //   8100800 2040000 200001 2440000 200002 2840000 880020104 4000000 7*0 40000400 8100800 2040000 200001
  //   2440000 200002 2840000 880020104 4000000 7*0 40000400 8100800 2040000 200001 2440000 200002 2840000
  //   880020104 4000000 7*0 40000400 8100800 2040000 200001 2440000 200002 2840000 880020104 4000000 7*0
  //   40000400 8100800 2040000 200001 2440000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
endmodule

module MEMORY_UNIT (
  input  [15:0] MEMIN,
  input  MOE,
  input  SPOE,
  input  SPE,
  input  SWE,
  input  ADWE,
  input  MWE,
  input  D_U,
  input  CE,
  input  CLK,
  input  MR,
  output [15:0] MEMOUT,
  output [7:0] SP,
  output [15:0] MEMAD
);

  wire and_1_out, controlled_buffer_3_out, controlled_buffer_4_out, controlled_buffer_5_out, not_1_out;
  wire [7:0] bit_extender_1_out;
  wire [14:0] bit_extender_3_out, bit_extender_4_out, controlled_buffer_2_out, controlled_buffer_6_out,
       multiplexer_2_out;
  wire [15:0] bit_extender_2_out, controlled_buffer_1_out;

  Bit_Extender #(.in_width(16), .out_width(8), .\type ("zero")) bit_extender_1 (.in(MEMIN), .out(bit_extender_1_out));
  Counter counter_1 (
    .load(SWE), .D(bit_extender_1_out), .count(CE), .Q(SP), .up(D_U), .clk(CLK), .clr(MR));  // open: carry
  assign controlled_buffer_1_out = MWE ? MEMIN : 16'bz;  // Controlled_Buffer controlled_buffer_1
  Register #(.width(16)) register_1 (.D(MEMIN), .en(ADWE), .clk(CLK), .Q(MEMAD), .clr(MR));
  Multiplexer #(.disabled("Z"), .enable("true"), .width(16)) multiplexer_1 (
    .in0(controlled_buffer_1_out), .in1(bit_extender_2_out), .out(MEMOUT), .sel(SPOE), .en(MOE));
  assign bit_extender_2_out = {{8{1'b0}}, SP};  // Bit_Extender bit_extender_2
  and and_1 (and_1_out, ~SPE, MEMAD[15]);  // AND_Gate
  Multiplexer #(.width(15)) multiplexer_2 (
    .in0(bit_extender_4_out), .in1(bit_extender_3_out), .out(multiplexer_2_out), .sel(SPE));
  assign bit_extender_3_out = {{7{1'b0}}, SP};  // Bit_Extender bit_extender_3
  Bit_Extender #(.in_width(16), .out_width(15), .\type ("zero")) bit_extender_4 (.in(MEMAD), .out(bit_extender_4_out));
  RAM #(.addrWidth(15), .asyncread("true"), .clearpin("true"), .dataWidth(16), .databus("bidir")) ram_1 (
    .addr(controlled_buffer_2_out), .we(controlled_buffer_3_out), .oe(controlled_buffer_4_out),
    .clk(controlled_buffer_5_out), .data(controlled_buffer_1_out), .clr(MR));
  assign controlled_buffer_2_out = not_1_out ? multiplexer_2_out : 15'bz;  // Controlled_Buffer controlled_buffer_2
  not not_1 (not_1_out, and_1_out);
  assign controlled_buffer_3_out = not_1_out ? MWE : 1'bz;  // Controlled_Buffer controlled_buffer_3
  assign controlled_buffer_4_out = not_1_out ? MOE : 1'bz;  // Controlled_Buffer controlled_buffer_4
  assign controlled_buffer_5_out = not_1_out ? CLK : 1'bz;  // Controlled_Buffer controlled_buffer_5
  ROM #(.addrWidth(15), .dataWidth(16)) rom_1 (.addr(controlled_buffer_6_out), .data(controlled_buffer_1_out));
  assign controlled_buffer_6_out = and_1_out ? multiplexer_2_out : 15'bz;  // Controlled_Buffer controlled_buffer_6

  // Notes on the sheet:
  //   contents of rom_1 (hex, n*v repeats v):
  //   fa 178 1f8 79 7b 68 0 4e8 0 168 0 497 2917 4404 86f 5e2 40 68 0 4e8 0 168 0 67 32739*0 8011 8018 0 0
  //   8000
endmodule

module THE_CLOCK (
  input  SINGLE_STEP_IN,
  input  SINGLE_STEP,
  input  HLT,
  output CLK,
  output nCLK
);

  wire clock_1_out, multiplexer_1_out;

  Clock clock_1 (.out(clock_1_out));
  Multiplexer multiplexer_1 (.in0(SINGLE_STEP_IN), .in1(clock_1_out), .out(multiplexer_1_out), .sel(SINGLE_STEP));
  and and_1 (CLK, multiplexer_1_out, ~HLT);  // AND_Gate
  not not_1 (nCLK, CLK);
endmodule

module I_O_PORT (
  input  [7:0] ADDRESS,
  input  ADWE,
  input  CLK,
  input  MR,
  input  [7:0] DATA,
  input  in_6,
  input  [7:0] Q0_7
);

  wire decoder_1_out1, decoder_1_out2;
  wire [2:0] bit_extender_4_out;
  wire [3:0] bit_extender_1_out, register_1_q;
  wire [5:0] bit_extender_2_out, bit_extender_3_out, XPOS_q, YPOS_q;

  Bit_Extender #(.out_width(4), .\type ("zero")) bit_extender_1 (.in(ADDRESS), .out(bit_extender_1_out));
  Register #(.width(4)) register_1 (.D(bit_extender_1_out), .en(ADWE), .clk(CLK), .Q(register_1_q), .clr(MR));
  Decoder #(.select(4)) decoder_1 (
    .out1(decoder_1_out1), .out2(decoder_1_out2), .sel(register_1_q));  // open: out0, out3, out4, out5, out6, out7, out8, out9, out10, out11, out12, out13, out14, out15, en
  Register #(.width(6)) XPOS (.D(bit_extender_2_out), .en(decoder_1_out1), .clk(CLK), .Q(XPOS_q), .clr(MR));
  Bit_Extender #(.out_width(6), .\type ("zero")) bit_extender_2 (.in(DATA), .out(bit_extender_2_out));
  Register #(.width(6)) YPOS (.D(bit_extender_3_out), .en(decoder_1_out2), .clk(CLK), .Q(YPOS_q), .clr(MR));
  Bit_Extender #(.out_width(6), .\type ("zero")) bit_extender_3 (.in(DATA), .out(bit_extender_3_out));
  Decoder #(.select(3)) decoder_2 (.sel(bit_extender_4_out));  // open: out0, out1, out2, out3, out4, out5, out6, out7, en
  Bit_Extender #(.out_width(3), .\type ("zero")) bit_extender_4 (.in(Q0_7), .out(bit_extender_4_out));
  // RGB_Video #(.cursor("No Cursor"), .height(64), .scale(8), .width(64)) rgb_video_1: pin names not known; wires that end beside it: XPOS_q, YPOS_q
endmodule

module INTERRUPT (
  input  I,
  input  PINTE,
  input  [15:0] INT_IN,
  input  P0,
  input  P1,
  input  P2,
  input  P3,
  input  CLR,
  input  CLK,
  input  MR,
  output [31:0] DATA,
  output INT
);

  wire and_1_out, and_2_out, and_3_out, and_4_out, decoder_1_out0, decoder_1_out1, decoder_1_out2,
       decoder_1_out3, decoder_2_out0, decoder_2_out1, decoder_2_out2, decoder_2_out3, j_k_ff_1_q,
       j_k_ff_2_q, j_k_ff_3_q, j_k_ff_4_q, priority_encoder_1_en_out, register_1_q, register_2_q,
       register_3_q, register_4_q;
  wire [1:0] priority_encoder_1_out;

  Decoder #(.select(2)) decoder_1 (
    .out0(decoder_1_out0), .out1(decoder_1_out1), .out2(decoder_1_out2), .out3(decoder_1_out3),
    .sel(INT_IN[1:0]), .en(PINTE));
  Register #(.width(1)) register_1 (.D(I), .en(decoder_1_out0), .Q(register_1_q), .clk(CLK), .clr(MR));
  Register #(.width(1)) register_2 (.D(I), .en(decoder_1_out1), .Q(register_2_q), .clk(CLK), .clr(MR));
  Register #(.width(1)) register_3 (.D(I), .en(decoder_1_out2), .Q(register_3_q), .clk(CLK), .clr(MR));
  Register #(.width(1)) register_4 (.D(I), .en(decoder_1_out3), .Q(register_4_q), .clk(CLK), .clr(MR));
  Decoder #(.select(2)) decoder_2 (
    .out0(decoder_2_out0), .out1(decoder_2_out1), .out2(decoder_2_out2), .out3(decoder_2_out3),
    .sel(priority_encoder_1_out), .en(CLR));
  and and_1 (and_1_out, ~register_1_q, P0);  // AND_Gate
  and and_2 (and_2_out, ~register_2_q, P1);  // AND_Gate
  and and_3 (and_3_out, ~register_3_q, P2);  // AND_Gate
  and and_4 (and_4_out, ~register_4_q, P3);  // AND_Gate
  J_K_Flip_Flop j_k_ff_1 (
    .J(1'b0), .clk(CLK), .K(decoder_2_out0), .Q(j_k_ff_1_q), .preset(and_1_out), .reset(MR));  // open: Qn
  J_K_Flip_Flop j_k_ff_2 (
    .J(1'b0), .clk(CLK), .K(decoder_2_out1), .Q(j_k_ff_2_q), .preset(and_2_out), .reset(MR));  // open: Qn
  J_K_Flip_Flop j_k_ff_3 (
    .J(1'b0), .clk(CLK), .K(decoder_2_out2), .Q(j_k_ff_3_q), .preset(and_3_out), .reset(MR));  // open: Qn
  J_K_Flip_Flop j_k_ff_4 (
    .J(1'b0), .clk(CLK), .K(decoder_2_out3), .Q(j_k_ff_4_q), .preset(and_4_out), .reset(MR));  // open: Qn
  not not_1 (INT, priority_encoder_1_en_out);
  LED led_1 (.in(priority_encoder_1_out[1]));
  LED led_2 (.in(priority_encoder_1_out[0]));
  Priority_Encoder #(.select(2)) priority_encoder_1 (
    .in0(j_k_ff_1_q), .in1(j_k_ff_2_q), .in2(j_k_ff_3_q), .in3(j_k_ff_4_q), .out(priority_encoder_1_out),
    .en_out(priority_encoder_1_en_out));  // open: gs, en_in
  Multiplexer #(.select(2), .width(16)) multiplexer_1 (
    .in0(16'hfffb), .in1(16'hfffc), .in2(16'hfffd), .in3(16'hfffe), .out(DATA[22:7]),
    .sel(priority_encoder_1_out));

  assign {DATA[31:23], DATA[6:0]} = 16'h2;
endmodule

module PORTS (
  input  MR,
  input  P0WE,
  input  CLK,
  input  [15:0] P0D,
  input  PWE,
  input  [15:0] PORTIN,
  input  PADWE,
  input  POE,
  input  P1WE,
  input  [15:0] P1D,
  input  P2WE,
  input  [15:0] P2D,
  input  P3WE,
  input  [15:0] P3D,
  output P0I,
  output [15:0] P0Q,
  output P1I,
  output [15:0] P1Q,
  output P2I,
  output [15:0] P2Q,
  output P3I,
  output [15:0] P3Q,
  output [15:0] POUT
);

  wire decoder_1_out0, decoder_1_out1, decoder_1_out2, decoder_1_out3, multiplexer_2_out, multiplexer_4_out,
       multiplexer_6_out, multiplexer_8_out;
  wire [1:0] bit_extender_1_out;
  wire [15:0] multiplexer_1_out, multiplexer_3_out, multiplexer_5_out, multiplexer_7_out, register_1_q;

  Register #(.width(16)) register_1 (.D(PORTIN), .en(PADWE), .clk(CLK), .Q(register_1_q), .clr(MR));
  Decoder #(.disabled("Z"), .select(2)) decoder_1 (
    .out0(decoder_1_out0), .out1(decoder_1_out1), .out2(decoder_1_out2), .out3(decoder_1_out3),
    .sel(bit_extender_1_out), .en(PWE));
  Pull_Resistor pull_resistor_1 (.node(decoder_1_out0));
  Pull_Resistor pull_resistor_2 (.node(decoder_1_out1));
  Pull_Resistor pull_resistor_3 (.node(decoder_1_out2));
  Pull_Resistor pull_resistor_4 (.node(decoder_1_out3));
  Bit_Extender #(.in_width(16), .out_width(2), .\type ("zero")) bit_extender_1 (
    .in(register_1_q), .out(bit_extender_1_out));
  Multiplexer #(.width(16)) multiplexer_1 (.in0(P0D), .in1(PORTIN), .out(multiplexer_1_out), .sel(decoder_1_out0));
  Multiplexer multiplexer_2 (.in0(P0WE), .in1(decoder_1_out0), .out(multiplexer_2_out), .sel(decoder_1_out0));
  Multiplexer #(.width(16)) multiplexer_3 (.in0(P1D), .in1(PORTIN), .out(multiplexer_3_out), .sel(decoder_1_out1));
  Multiplexer multiplexer_4 (.in0(P1WE), .in1(decoder_1_out1), .out(multiplexer_4_out), .sel(decoder_1_out1));
  Multiplexer #(.width(16)) multiplexer_5 (.in0(P2D), .in1(PORTIN), .out(multiplexer_5_out), .sel(decoder_1_out2));
  Multiplexer multiplexer_6 (.in0(P2WE), .in1(decoder_1_out2), .out(multiplexer_6_out), .sel(decoder_1_out2));
  Multiplexer #(.width(16)) multiplexer_7 (.in0(P3D), .in1(PORTIN), .out(multiplexer_7_out), .sel(decoder_1_out3));
  Multiplexer multiplexer_8 (.in0(P3WE), .in1(decoder_1_out3), .out(multiplexer_8_out), .sel(decoder_1_out3));
  Register #(.width(16)) register_2 (.D(multiplexer_1_out), .en(multiplexer_2_out), .clk(CLK), .Q(P0Q), .clr(MR));
  Register #(.width(16)) register_3 (.D(multiplexer_3_out), .en(multiplexer_4_out), .clk(CLK), .Q(P1Q), .clr(MR));
  Register #(.width(16)) register_4 (.D(multiplexer_5_out), .en(multiplexer_6_out), .clk(CLK), .Q(P2Q), .clr(MR));
  Register #(.width(16)) register_5 (.D(multiplexer_7_out), .en(multiplexer_8_out), .clk(CLK), .Q(P3Q), .clr(MR));
  Multiplexer #(.disabled("Z"), .enable("true"), .select(2), .width(16)) multiplexer_9 (
    .in0(P0Q), .in1(P1Q), .in2(P2Q), .in3(P3Q), .out(POUT), .sel(bit_extender_1_out), .en(POE));

  assign P0I = P0WE;
  assign P1I = P1WE;
  assign P2I = P2WE;
  assign P3I = P3WE;
endmodule
